# Fritzing sketch ProximityChirp (saved by Fritzing 0.9.2b)

parts:
  Part1 = Arduino Uno (Rev3)
  J1 = Infrared Proximity Sensor
  SP1 = SPEAKER [package=pcb_mount_speaker]

nets:
  N1: Part1.A0, J1.Vout
  N2: Part1.D9_PWM, SP1.-
  GND: Part1.GND, J1.GND, SP1.+
  5V: Part1.5V, J1.Vcc
